// Logisim project harward_arc terminal.circ as structural Verilog: 11 circuits, main circuit 8 bit to 7 (-high)
module main (
);

  wire addr_fe_bit_7, and_1_out, and_2_out, and_3_out, and_4_out, and_5_out, button_1_out, button_2_out,
       cdm_8_mark5_1_data_inst, Cl, code, comparator_1_eq, comparator_2_eq, comparator_3_eq, comparator_4_eq,
       data, end_message, keyboard_1_avail, keyboard_2_clean, keyboard_2_increment_rundom_index,
       keyboard_2_keyboard_clock, keyboard_2_turn_off_on, keyboard_2_update_random_number_for_bot,
       keyboard_2_update_random_number_for_field, load_cell_1_out, load_cell_2_out, load_cell_3_out, mem,
       message_box_1_terminal_clean, message_box_1_terminal_clock, not_1_out, or_1_out, or_2_out, rd_wr,
       write_field_1_dicplay_clean, write_field_1_display_clock, write_field_2_dicplay_clean,
       write_field_2_display_clock;
  wire [1:0] store_cell_1_output;
  wire [3:0] number_of_living_cells_1_high, number_of_living_cells_1_low, number_of_living_cells_2_high,
       number_of_living_cells_2_low;
  wire [5:0] store_cell_1_output_2;
  wire [6:0] ascii_cod, message_box_1_ascii_code_out, write_field_1_ascii_code, write_field_2_ascii_code;
  wire [7:0] addr, addr_8_15, bot_s_cell, cdm_8_mark5_1_data_out, cdm_8_mark5_1_ps, cdm_8_mark5_1_r0,
       cdm_8_mark5_1_r1, cdm_8_mark5_1_r2, cdm_8_mark5_1_r3, cdm_8_mark5_1_sp, controlled_buffer_2_out,
       controlled_buffer_5_out, data_8_bit, keyboard_bits_in, keyboard_bits_out, random_number, register_2_q,
       register_3_q, undriven, undriven_2;
  wire [15:0] cdm_8_mark5_1_pc;
  wire [19:0] display_ship_1_out_2, display_ship_1_out_3, display_ship_1_out_4, display_ship_1_out_5,
       display_ship_1_out_6, display_ship_1_out_7, display_ship_1_out_8, display_ship_1_out_9,
       display_ship_1_out_10, display_ship_1_out_11, display_ship_1_out_12, display_ship_1_out_13,
       display_ship_1_out_14, display_ship_1_out_15, display_ship_1_out_16, display_ship_1_out_17,
       display_ship_1_out_18, display_ship_1_out_19, display_ship_1_out_20, display_ship_1_out_21,
       display_ship_1_out_22, display_ship_1_out_23, display_ship_1_out_24, display_ship_1_out_25,
       display_ship_1_out_26, display_ship_1_out_27, display_ship_1_out_28, display_ship_1_out_29,
       display_ship_1_out_30, display_ship_1_out_31, display_ship_1_out_32, display_ship_1_out_33;

  // Probe on cdm_8_mark5_1_r0
  // Probe on cdm_8_mark5_1_r1
  // Probe on cdm_8_mark5_1_r3
  // Probe on cdm_8_mark5_1_r2
  Clock clock_1 (.out(Cl));
  // Probe on cdm_8_mark5_1_sp
  // Probe on cdm_8_mark5_1_pc
  // Probe on cdm_8_mark5_1_ps
  CdM_8_mark5 cdm_8_mark5_1 (
    .clock(Cl), .addr({addr_8_15, addr}), .mem_read(rd_wr), .mem_cycle(mem),
    .data_inst(cdm_8_mark5_1_data_inst), .data_out(cdm_8_mark5_1_data_out),
    .data_in(controlled_buffer_2_out), .r0(cdm_8_mark5_1_r0), .r1(cdm_8_mark5_1_r1), .r2(cdm_8_mark5_1_r2),
    .r3(cdm_8_mark5_1_r3), .PC(cdm_8_mark5_1_pc), .SP(cdm_8_mark5_1_sp), .PS(cdm_8_mark5_1_ps));  // open: IAck, IRQ, vec, halted
  Comparator comparator_1 (.a(addr_8_15), .b({8{1'b0}}), .eq(comparator_1_eq));  // open: gt, lt
  Comparator comparator_2 (.a(8'hfe), .b(addr), .eq(comparator_2_eq));  // open: gt, lt
  // Probe on cdm_8_mark5_1_data_out
  and and_1 (and_1_out, comparator_1_eq, data, comparator_2_eq);
  Comparator comparator_3 (.a(8'h7), .b(addr), .eq(comparator_3_eq));  // open: gt, lt
  assign data_8_bit = not_1_out ? cdm_8_mark5_1_data_out : 8'bz;  // Controlled_Buffer controlled_buffer_1
  not not_1 (not_1_out, rd_wr);
  assign controlled_buffer_2_out = rd_wr ? data_8_bit : 8'bz;  // Controlled_Buffer controlled_buffer_2
  and and_2 (and_2_out, ~rd_wr, data, comparator_3_eq);  // AND_Gate
  Decoder #(.disabled(0)) decoder_1 (.out0(code), .out1(data), .sel(cdm_8_mark5_1_data_inst), .en(mem));
  Register register_1 (.D(data_8_bit), .en(and_1_out), .Q(keyboard_bits_in), .clk(Cl));  // open: clr
  Register register_2 (.D(undriven), .en(and_2_out), .Q(register_2_q), .clk(Cl));  // open: clr
  Comparator comparator_4 (.a(8'h8), .b(addr), .eq(comparator_4_eq));  // open: gt, lt
  // Probe on {addr_8_15, addr}
  load_cell load_cell_1 (.rd_wr(rd_wr), .data(data), .\const (8'hf8), .addr(addr), .out(load_cell_1_out));
  and and_3 (and_3_out, rd_wr, data, comparator_4_eq);
  assign data_8_bit = and_4_out ? keyboard_bits_out : 8'bz;  // Controlled_Buffer controlled_buffer_3
  and and_4 (and_4_out, rd_wr, data, comparator_2_eq);
  assign data_8_bit = load_cell_1_out ? random_number : 8'bz;  // Controlled_Buffer controlled_buffer_4
  assign controlled_buffer_5_out = and_3_out ? register_3_q : 8'bz;  // Controlled_Buffer controlled_buffer_5
  Register register_3 (.D(undriven_2), .en(and_3_out), .Q(register_3_q), .clk(Cl));  // open: clr
  load_cell load_cell_2 (.rd_wr(rd_wr), .data(data), .\const (8'hfb), .addr(addr), .out(load_cell_2_out));
  and and_5 (and_5_out, ~or_1_out, data);  // AND_Gate
  or or_1 (or_1_out, and_4_out, load_cell_1_out, load_cell_2_out, load_cell_3_out);
  assign data_8_bit = load_cell_2_out ? bot_s_cell : 8'bz;  // Controlled_Buffer controlled_buffer_6
  write_field write_field_1 (
    .rd_wr(rd_wr), .data_1_bit(data), .bot_user_adress(8'hfc), .addr(addr), .data_8_bit(data_8_bit),
    .ASCII_code(write_field_1_ascii_code), .display_clock(write_field_1_display_clock),
    .dicplay_clean(write_field_1_dicplay_clean));
  TTY #(.rows(12), .cols(13)) tty_1 (
    .data(write_field_1_ascii_code), .clk(write_field_1_display_clock), .clr(write_field_1_dicplay_clean));  // open: we
  // RAM ram_1: pin names not known; wires that end beside it: {addr_8_15, addr}, code, 1'b1, data_8_bit
  // RAM ram_2: pin names not known; wires that end beside it: addr, and_5_out, Cl, rd_wr, data_8_bit
  load_cell load_cell_3 (.rd_wr(rd_wr), .data(data), .\const (8'hfd), .addr(addr), .out(load_cell_3_out));
  Hex_Digit_Display hex_digit_display_1 (.value(number_of_living_cells_1_low));  // open: dp
  Hex_Digit_Display hex_digit_display_2 (.value(number_of_living_cells_1_high));  // open: dp
  number_of_living_cells number_of_living_cells_1 (
    .data_8_bit(data_8_bit), .rd_wr(rd_wr), .data_1_bit(data), .Cl(Cl), .\const (8'hf0), .addr(addr),
    .low(number_of_living_cells_1_low), .high(number_of_living_cells_1_high));
  assign data_8_bit = load_cell_3_out ? {1'b0, ascii_cod} : 8'bz;  // Controlled_Buffer controlled_buffer_7
  // Probe on {1'b0, ascii_cod}
  message_box message_box_1 (
    .clock(Cl), .data_8_bit(data_8_bit), .rd_wr(rd_wr), .data_1_bit(data), .addr(addr),
    .ASCII_code_out(message_box_1_ascii_code_out), .terminal_clock(message_box_1_terminal_clock),
    .terminal_clean(message_box_1_terminal_clean), .end_message(end_message),
    .addr_fe__bit___7(addr_fe_bit_7), .buttom(button_1_out));
  TTY #(.cols(50)) tty_2 (
    .data(message_box_1_ascii_code_out), .clk(message_box_1_terminal_clock),
    .clr(message_box_1_terminal_clean));  // open: we
  Button button_1 (.out(button_1_out));
  display_ship display_ship_1 (
    .num_picture(store_cell_1_output), .out_2(display_ship_1_out_2), .out_3(display_ship_1_out_3),
    .out_4(display_ship_1_out_4), .out_5(display_ship_1_out_5), .out_6(display_ship_1_out_6),
    .out_7(display_ship_1_out_7), .out_8(display_ship_1_out_8), .out_9(display_ship_1_out_9),
    .out_10(display_ship_1_out_10), .out_11(display_ship_1_out_11), .out_12(display_ship_1_out_12),
    .out_13(display_ship_1_out_13), .out_14(display_ship_1_out_14), .out_15(display_ship_1_out_15),
    .out_16(display_ship_1_out_16), .out_17(display_ship_1_out_17), .out_18(display_ship_1_out_18),
    .out_19(display_ship_1_out_19), .out_20(display_ship_1_out_20), .out_21(display_ship_1_out_21),
    .out_22(display_ship_1_out_22), .out_23(display_ship_1_out_23), .out_24(display_ship_1_out_24),
    .out_25(display_ship_1_out_25), .out_26(display_ship_1_out_26), .out_27(display_ship_1_out_27),
    .out_28(display_ship_1_out_28), .out_29(display_ship_1_out_29), .out_30(display_ship_1_out_30),
    .out_31(display_ship_1_out_31), .out_32(display_ship_1_out_32), .out_33(display_ship_1_out_33));
  DotMatrix #(.matrixcols(32), .matrixrows(20)) dotmatrix_1 (
    .col0(display_ship_1_out_2), .col1(display_ship_1_out_3), .col2(display_ship_1_out_4),
    .col3(display_ship_1_out_5), .col4(display_ship_1_out_6), .col5(display_ship_1_out_7),
    .col6(display_ship_1_out_8), .col7(display_ship_1_out_9), .col8(display_ship_1_out_10),
    .col9(display_ship_1_out_11), .col10(display_ship_1_out_12), .col11(display_ship_1_out_13),
    .col12(display_ship_1_out_14), .col13(display_ship_1_out_15), .col14(display_ship_1_out_16),
    .col15(display_ship_1_out_17), .col16(display_ship_1_out_18), .col17(display_ship_1_out_19),
    .col18(display_ship_1_out_20), .col19(display_ship_1_out_21), .col20(display_ship_1_out_22),
    .col21(display_ship_1_out_23), .col22(display_ship_1_out_24), .col23(display_ship_1_out_25),
    .col24(display_ship_1_out_26), .col25(display_ship_1_out_27), .col26(display_ship_1_out_28),
    .col27(display_ship_1_out_29), .col28(display_ship_1_out_30), .col29(display_ship_1_out_31),
    .col30(display_ship_1_out_32), .col31(display_ship_1_out_33));
  Keyboard #(.buflen(4)) keyboard_1 (
    .clk(keyboard_2_keyboard_clock), .re(keyboard_2_turn_off_on), .clr(or_2_out), .avail(keyboard_1_avail),
    .data(ascii_cod));
  or or_2 (or_2_out, keyboard_2_clean, button_2_out);
  Button button_2 (.out(button_2_out));
  random_field random_field_1 (
    .cl(Cl), .cell_data(bot_s_cell), .update_register(keyboard_2_update_random_number_for_field),
    .update_counter(keyboard_2_increment_rundom_index));
  random_number random_number_1 (
    .cl(Cl), .cell_data(random_number),
    .update_random_number_for_field(keyboard_2_update_random_number_for_bot));
  keyboard keyboard_2 (
    .empty_keyboard(keyboard_1_avail), .keyboard_bits_in(keyboard_bits_in), .end_message(end_message),
    .addr_fe_bit_7(addr_fe_bit_7), .keyboard_bits_out(keyboard_bits_out),
    .keyboard_clock(keyboard_2_keyboard_clock), .turn_off_on(keyboard_2_turn_off_on),
    .clean(keyboard_2_clean), .update_random_number_for_field(keyboard_2_update_random_number_for_field),
    .increment_rundom_index(keyboard_2_increment_rundom_index),
    .update_random_number_for_bot(keyboard_2_update_random_number_for_bot));
  store_cell store_cell_1 (
    .rd_wr(rd_wr), .data_8_bit(data_8_bit), .data_1_bit(data), .\const (8'hf9), .addr(addr), .cl(Cl),
    .\output ({store_cell_1_output_2, store_cell_1_output}));
  write_field write_field_2 (
    .rd_wr(rd_wr), .data_1_bit(data), .bot_user_adress(8'hfa), .addr(addr), .data_8_bit(data_8_bit),
    .ASCII_code(write_field_2_ascii_code), .display_clock(write_field_2_display_clock),
    .dicplay_clean(write_field_2_dicplay_clean));
  TTY #(.rows(12), .cols(13)) tty_3 (
    .data(write_field_2_ascii_code), .clk(write_field_2_display_clock), .clr(write_field_2_dicplay_clean));  // open: we
  Hex_Digit_Display hex_digit_display_3 (.value(number_of_living_cells_2_low));  // open: dp
  Hex_Digit_Display hex_digit_display_4 (.value(number_of_living_cells_2_high));  // open: dp
  number_of_living_cells number_of_living_cells_2 (
    .data_8_bit(data_8_bit), .rd_wr(rd_wr), .data_1_bit(data), .Cl(Cl), .\const (8'hf1), .addr(addr),
    .low(number_of_living_cells_2_low), .high(number_of_living_cells_2_high));

  // Notes on the sheet:
  //   Терминал вывода поля пользователя
  //   Red Button
  //   терминал общения с пользователем
  //   clean button
  //   Терминал вывода поля бота
endmodule

module _8_bit_to_7___high (
  input  [7:0] entrance,
  output [6:0] bus_0
);


  assign bus_0 = entrance[6:0];
endmodule

module message_box (
  input  clock,
  input  [7:0] data_8_bit,
  input  rd_wr,
  input  data_1_bit,
  input  [7:0] addr,
  input  buttom,
  input  addr_fe__bit___7,
  output [6:0] ASCII_code_out,
  output terminal_clock,
  output terminal_clean,
  output end_message
);

  wire and_1_out, and_3_out, and_5_out, cmp, comparator_1_eq, counter_1_carry, not_1_out, or_1_out, or_2_out,
       or_3_out, register_1_q, register_2_q;
  wire [3:0] counter_1_q;
  wire [7:0] counter_2_q, demultiplexer_1_out1, rom_1_data;

  and and_1 (and_1_out, data_1_bit, ~rd_wr);  // AND_Gate
  Demultiplexer #(.width(8), .enable("false")) demultiplexer_1 (
    .out1(demultiplexer_1_out1), .in(addr), .sel(and_1_out));  // open: out0
  Comparator comparator_1 (.a({8{1'b1}}), .b(demultiplexer_1_out1), .eq(comparator_1_eq));  // open: gt, lt
  and and_2 (terminal_clean, ~rd_wr, data_1_bit, comparator_1_eq);  // AND_Gate
  not not_1 (not_1_out, terminal_clean);
  and and_3 (and_3_out, terminal_clean, clock);
  Counter #(.width(4), .max('hf), .trigger("falling")) counter_1 (
    .Q(counter_1_q), .carry(counter_1_carry), .clk(terminal_clock), .clr(terminal_clean));  // open: load, D, count
  Counter #(.trigger("falling")) counter_2 (
    .load(terminal_clean), .D(data_8_bit), .count(not_1_out), .Q(counter_2_q), .clk(or_1_out));  // open: carry, clr
  or or_1 (or_1_out, and_3_out, counter_1_carry);
  or or_2 (or_2_out, register_1_q, cmp);
  Register #(.width(1)) register_1 (.D(or_2_out), .Q(register_1_q), .clk(clock), .clr(terminal_clean));  // open: en
  ROM #(.addrWidth(12)) rom_1 (.addr({counter_2_q, counter_1_q}), .data(rom_1_data), .sel(1'b1));
  and and_4 (terminal_clock, ~register_1_q, clock);  // AND_Gate
  _8_bit_to_7___high u_8_bit_to_7_high_1 (.entrance(rom_1_data), .bus_0(ASCII_code_out));
  Comparator #(.width(7)) comparator_2 (.a(ASCII_code_out), .b({7{1'b0}}), .eq(cmp));  // open: gt, lt
  or or_3 (or_3_out, register_2_q, buttom);
  and and_5 (and_5_out, or_3_out, ~addr_fe__bit___7);  // AND_Gate
  Register #(.width(1)) register_2 (.D(and_5_out), .Q(register_2_q), .clk(clock));  // open: en, clr
  and and_6 (end_message, cmp, register_2_q);

  // Other names for the same wires on the sheet: Cl = clock; cl_input = terminal_clock; cmp_res = terminal_clean

  // Notes on the sheet:
  //   эта часть для загрузки адреса
  //   ___
  //   >
  //   ^
  //   |
  //   Эта часть для увеличения счётчика адреса
  //   4 младших за само сообщение
  //   8 старших за номер сообщения
  //   contents of rom_1 (hex, n*v repeats v):
  //   54 68 69 73 20 67 61 6d 65 20 69 73 20 22 53 65 61 20 42 61 74 74 6c 65 22 21 a 48 61 76 65 20 61 20
  //   67 6f 6f 64 20 74 69 6d 65 21 6*a 43 6c 69 63 6b 20 74 68 65 20 22 52 65 64 20 42 75 74 74 6f 6e 22
  //   20 74 6f 20 63 6f 6e 74 69 6e 75 65 2e 11*0 57 65 6c 6c 2c 20 77 65 20 6e 65 65 64 20 74 6f 20 61 72
  //   72 61 6e 67 65 20 74 68 65 20 73 68 69 70 73 2e a 54 68 65 72 65 20 69 73 20 61 20 6b 65 79 62 6f 61
  //   72 64 20 62 65 6c 6f 77 2e a 45 6e 74 65 72 20 74 68 65 20 63 6f 6f 72 64 69 6e 61 74 65 73 20 6f 66
  //   20 74 68 65 20 73 68 69 70 73 a 49 20 77 69 6c 6c 20 61 73 6b 20 66 6f 72 2e a 46 69 72 73 74 20 61
  //   20 6c 65 74 74 65 72 2c 20 74 68 65 6e 20 61 20 64 69 67 69 74 2e a 46 6f 72 20 65 78 61 6d 70 6c 65
  //   3a 20 41 32 20 6f 72 20 61 32 a a 43 6c 69 63 6b 20 74 68 65 20 22 52 65 64 20 42 75 74 74 6f 6e 22
  //   20 74 6f 20 63 6f 6e 74 69 6e 75 65 2e 6*0 53 68 69 70 73 20 63 61 6e 6e 6f 74 20 62 65 20 6e 65 69
  //   67 68 62 6f 72 73 2e a 59 6f 75 20 77 69 6c 6c 20 68 61 76 65 3a a 31 20 73 68 69 70 20 77 69 74 68
  //   20 61 20 6c 65 6e 67 74 68 20 6f 66 20 34 2e a 32 20 73 68 69 70 73 20 33 20 69 6e 20 6c 65 6e 67 74
  //   68 2e a 33 20 73 68 69 70 73 20 32 20 69 6e 20 6c 65 6e 67 74 68 2e a 34 20 73 68 69 70 73 20 31 20
  //   69 6e 20 6c 65 6e 67 74 68 2e a a 43 6c 69 63 6b 20 74 68 65 20 22 52 65 64 20 42 75 74 74 6f 6e 22
  //   20 74 6f 20 63 6f 6e 74 69 6e 75 65 2e 8*0 45 6e 74 65 72 20 74 68 65 20 66 69 72 73 74 20 63 6f 6f
  //   72 64 69 6e 61 74 65 a 6f 66 20 74 68 65 20 73 68 69 70 20 6f 66 20 6c 65 6e 67 74 68 20 34 6*a 43
  //   6c 69 63 6b 20 74 68 65 20 22 52 65 64 20 42 75 74 74 6f 6e 22 20 74 6f 20 63 6f 6e 74 69 6e 75 65
  //   2e 5*0 45 6e 74 65 72 20 74 68 65 20 73 65 63 6f 6e 64 20 63 6f 6f 72 64 69 6e 61 74 65 a 6f 66 20
  //   74 68 65 20 73 68 69 70 20 6f 66 20 6c 65 6e 67 74 68 20 34 6*a 43 6c 69 63 6b 20 74 68 65 20 22 52
  //   65 64 20 42 75 74 74 6f 6e 22 20 74 6f 20 63 6f 6e 74 69 6e 75 65 2e 4*0 45 6e 74 65 72 20 74 68 65
  //   20 66 69 72 73 74 20 63 6f 6f 72 64 69 6e 61 74 65 a 6f 66 20 74 68 65 20 73 68 69 70 20 6f 66 20 6c
  //   65 6e 67 74 68 20 33 6*a 43 6c 69 63 6b 20 74 68 65 20 22 52 65 64 20 42 75 74 74 6f 6e 22 20 74 6f
  //   20 63 6f 6e 74 69 6e 75 65 2e 5*0 45 6e 74 65 72 20 74 68 65 20 73 65 63 6f 6e 64 20 63 6f 6f 72 64
  //   69 6e 61 74 65 a 6f 66 20 74 68 65 20 73 68 69 70 20 6f 66 20 6c 65 6e 67 74 68 20 33 6*a 43 6c 69
  //   63 6b 20 74 68 65 20 22 52 65 64 20 42 75 74 74 6f 6e 22 20 74 6f 20 63 6f 6e 74 69 6e 75 65 2e 4*0
  //   45 6e 74 65 72 20 74 68 65 20 66 69 72 73 74 20 63 6f 6f 72 64 69 6e 61 74 65 a 6f 66 20 74 68 65 20
  //   73 68 69 70 20 6f 66 20 6c 65 6e 67 74 68 20 32 6*a 43 6c 69 63 6b 20 74 68 65 20 22 52 65 64 20 42
  //   75 74 74 6f 6e 22 20 74 6f 20 63 6f 6e 74 69 6e 75 65 2e 5*0 45 6e 74 65 72 20 74 68 65 20 73 65 63
  //   6f 6e 64 20 63 6f 6f 72 64 69 6e 61 74 65 a 6f 66 20 74 68 65 20 73 68 69 70 20 6f 66 20 6c 65 6e 67
  //   74 68 20 32 6*a 43 6c 69 63 6b 20 74 68 65 20 22 52 65 64 20 42 75 74 74 6f 6e 22 20 74 6f 20 63 6f
  //   6e 74 69 6e 75 65 2e 4*0 45 6e 74 65 72 20 6f 6e 65 20 63 6f 6f 72 64 69 6e 61 74 65 20 66 6f 72 20
  //   61 20 73 68 69 70 20 6f 66 20 6c 65 6e 67 74 68 20 31 6*a 43 6c 69 63 6b 20 74 68 65 20 22 52 65 64
  //   20 42 75 74 74 6f 6e 22 20 74 6f 20 63 6f 6e 74 69 6e 75 65 2e 12*0 54 68 65 20 66 69 65 6c 64 20 69
  //   73 20 62 65 69 6e 67 20 70 72 69 6e 74 65 64 2e a 50 6c 65 61 73 65 20 77 61 69 74 21 a 20 20 20 50
  //   6c 65 61 73 65 20 77 61 69 74 21 a 6*20 50 6c 65 61 73 65 20 77 61 69 74 21 a 9*20 50 6c 65 61 73 65
  //   20 77 61 69 74 21 a 12*20 50 6c 65 61 73 65 20 77 61 69 74 21 a 15*20 50 6c 65 61 73 65 20 77 61 69
  //   74 21 a 18*20 50 6c 65 61 73 65 20 77 61 69 74 21 11*0 59 6f 75 20 68 61 76 65 20 65 6e 74 65 72 65
  //   64 20 61 6e 20 69 6e 63 6f 72 72 65 63 74 20 73 79 6d 62 6f 6c 73 2e a 50 6c 65 61 73 65 20 74 72 79
  //   20 61 67 61 69 6e 2e 6*a 43 6c 69 63 6b 20 74 68 65 20 22 52 65 64 20 42 75 74 74 6f 6e 22 20 74 6f
  //   20 63 6f 6e 74 69 6e 75 65 2e 15*0 59 6f 75 20 68 61 76 65 20 65 6e 74 65 72 65 64 20 63 6f 6f 72 64
  //   69 6e 61 74 65 73 a 6f 66 20 69 6e 63 6f 72 72 65 63 74 20 6c 65 6e 67 74 68 2e a 50 6c 65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
endmodule

module write_field (
  input  rd_wr,
  input  data_1_bit,
  input  [7:0] bot_user_adress,
  input  [7:0] addr,
  input  [7:0] data_8_bit,
  output display_clock,
  output dicplay_clean,
  output [6:0] ASCII_code
);

  wire and_1_out, and_2_out, and_3_out, comparator_1_eq, comparator_2_eq;
  wire [7:0] demultiplexer_1_out1;

  Demultiplexer #(.width(8), .enable("false")) demultiplexer_1 (
    .out1(demultiplexer_1_out1), .in(addr), .sel(and_1_out));  // open: out0
  Comparator comparator_1 (.a(bot_user_adress), .b(demultiplexer_1_out1), .eq(comparator_1_eq));  // open: gt, lt
  and and_1 (and_1_out, data_1_bit, ~rd_wr);  // AND_Gate
  and and_2 (and_2_out, ~rd_wr, data_1_bit, and_3_out);  // AND_Gate
  and and_3 (and_3_out, and_1_out, comparator_1_eq);
  and and_4 (display_clock, 1'b1, and_2_out);
  // Probe on data_8_bit
  Multiplexer #(.select(5), .width(7), .enable("false")) multiplexer_1 (
    .in0(7'b1111110), .in1(7'b0100011), .in2(7'b0100001), .in3(7'b1011000), .in4(7'b1101111),
    .in5(7'b0100000), .in6(7'b0110000), .in7(7'b0110001), .in8(7'b0110010), .in9(7'b0110011),
    .in10(7'b0110100), .in11(7'b0110101), .in12(7'b0110110), .in13(7'b0110111), .in14(7'b0111000),
    .in15(7'b0111001), .in16(7'b1000001), .in17(7'b1000010), .in18(7'b1000011), .in19(7'b1000100),
    .in20(7'b1000101), .in21(7'b1000110), .in22(7'b1000111), .in23(7'b1001000), .in24(7'b1001001),
    .in25(7'b1001010), .in26(7'b0001101), .in27(7'b0100011), .in28(7'b0100000), .in29(7'b0100000),
    .in30(7'b0100000), .in31({7{1'b0}}), .out(ASCII_code), .sel(data_8_bit[4:0]));
  Comparator comparator_2 (.a(8'h1f), .b(data_8_bit), .eq(comparator_2_eq));  // open: gt, lt
  and and_5 (dicplay_clean, display_clock, comparator_2_eq);
  TTY #(.rows(12), .cols(13)) tty_1 (.data(ASCII_code), .clk(display_clock), .clr(dicplay_clean));  // open: we
  // Probe on ASCII_code

  // Notes on the sheet:
  //   для очистки дисплея 31
  //   0 - ничего (~)
  //   1 - корабль (#)
  //   2 - занято (!)
  //   5 - пробел
  //   27 - корабль, но на поле бота (~)
  //   3 - подбитый корабль (X)
  //   4 - выстрел в ничего (* или +)
  //   6 - 15 = figures
  //   16 - 25 = letters
  //   26 - '\n' (Enter)
endmodule

module number_of_living_cells (
  input  [7:0] data_8_bit,
  input  rd_wr,
  input  data_1_bit,
  input  Cl,
  input  [7:0] \const ,
  input  [7:0] addr,
  output [3:0] high,
  output [3:0] low
);

  wire and_1_out, comparator_1_eq;
  wire [7:0] register_1_q;
  wire [7:4] divider_1_out, divider_1_rem;

  Comparator comparator_1 (.a(\const ), .b(addr), .eq(comparator_1_eq));  // open: gt, lt
  and and_1 (and_1_out, ~rd_wr, data_1_bit, comparator_1_eq);  // AND_Gate
  Register register_1 (.D(data_8_bit), .en(and_1_out), .Q(register_1_q), .clk(Cl));  // open: clr
  Divider divider_1 (
    .a(register_1_q), .b(8'ha), .out({divider_1_out, high}), .rem({divider_1_rem, low}));  // open: upper
endmodule

module store_cell (
  input  rd_wr,
  input  [7:0] data_8_bit,
  input  data_1_bit,
  input  [7:0] \const ,
  input  cl,
  input  [7:0] addr,
  output [7:0] \output 
);

  wire and_1_out, comparator_1_eq;

  Comparator comparator_1 (.a(\const ), .b(addr), .eq(comparator_1_eq));  // open: gt, lt
  and and_1 (and_1_out, ~rd_wr, data_1_bit, comparator_1_eq);  // AND_Gate
  Register register_1 (.D(data_8_bit), .en(and_1_out), .Q(\output ), .clk(cl));  // open: clr
endmodule

module load_cell (
  input  rd_wr,
  input  data,
  input  [7:0] \const ,
  input  [7:0] addr,
  output out
);

  wire comparator_1_eq;

  Comparator comparator_1 (.a(\const ), .b(addr), .eq(comparator_1_eq));  // open: gt, lt
  and and_1 (out, rd_wr, data, comparator_1_eq);
endmodule

module keyboard (
  input  empty_keyboard,
  input  [7:0] keyboard_bits_in,
  input  end_message,
  output keyboard_clock,
  output turn_off_on,
  output clean,
  output [7:0] keyboard_bits_out,
  output addr_fe_bit_7,
  output update_random_number_for_field,
  output increment_rundom_index,
  output update_random_number_for_bot
);


  assign addr_fe_bit_7 = keyboard_bits_in[7];
  assign clean = keyboard_bits_in[2];
  assign increment_rundom_index = keyboard_bits_in[5];
  assign keyboard_bits_out = {end_message, 3'b000, empty_keyboard, keyboard_bits_in[2:0]};
  assign keyboard_clock = keyboard_bits_in[0];
  assign turn_off_on = keyboard_bits_in[1];
  assign update_random_number_for_bot = keyboard_bits_in[4];
  assign update_random_number_for_field = keyboard_bits_in[6];
endmodule

module random_field (
  input  cl,
  input  update_register,
  input  update_counter,
  output [7:0] cell_data
);

  wire [7:0] counter_1_q, register_1_q;
  wire [11:0] adder_1_out, counter_2_q, multiplier_1_out;

  Counter #(.max('h27)) counter_1 (.Q(counter_1_q), .clk(cl));  // open: load, D, count, carry, clr
  Register register_1 (.D(counter_1_q), .Q(register_1_q), .clk(update_register));  // open: en, clr
  // Probe on {4'b0000, register_1_q}
  // Probe on multiplier_1_out
  Multiplier #(.width(12)) multiplier_1 (
    .a({4'b0000, register_1_q}), .b(12'h64), .out(multiplier_1_out));  // open: cin, cout
  Counter #(.width(12), .max('h63)) counter_2 (
    .Q(counter_2_q), .clk(update_counter));  // open: load, D, count, carry, clr
  // Probe on counter_2_q
  Adder #(.width(12)) adder_1 (.a(multiplier_1_out), .b(counter_2_q), .out(adder_1_out));  // open: cin, cout
  // Probe on adder_1_out
  ROM #(.addrWidth(12)) rom_1 (.addr(adder_1_out), .data(cell_data));  // open: sel

  // Notes on the sheet:
  //   contents of rom_1 (hex, n*v repeats v):
  //   0 0 1b 0 0 1b 1b 14*0 1b 0 1b 0 0 0 1b 9*0 1b 0 0 0 4*1b 17*0 1b 4*0 1b 0 1b 0 0 1b 6*0 1b 0 0 1b
  //   6*0 1b 5*0 1b 8*0 1b 0 1b 1b 18*0 1b 0 0 1b 9*0 1b 1b 0 0 0 1b 0 1b 1b 0 1b 1b 8*0 1b 1b 0 0 0 1b 0
  //   1b 7*0 1b 9*0 1b 5*0 1b 1b 8*0 1b 6*0 1b 0 1b 11*0 1b 1b 1b 17*0 1b 9*0 1b 0 1b 0 1b 1b 13*0 1b 1b 0
  //   1b 0 0 0 1b 5*0 1b 0 0 0 1b 5*0 1b 0 0 0 1b 12*0 1b 1b 1b 5*0 1b 5*0 1b 1b 1b 17*0 1b 0 0 0 1b 1b
  //   12*0 4*1b 0 0 1b 9*0 1b 0 0 1b 13*0 1b 1b 0 1b 0 0 0 1b 6*0 1b 1b 12*0 1b 1b 1b 0 0 1b 19*0 1b 7*0
  //   1b 0 1b 13*0 1b 7*0 1b 8*0 1b 1b 4*0 1b 1b 1b 0 1b 1b 0 0 1b 6*0 1b 6*0 1b 4*0 1b 1b 0 1b 15*0 1b 0
  //   0 1b 9*0 1b 7*0 1b 6*0 1b 0 0 1b 0 0 1b 1b 1b 0 1b 0 0 1b 6*0 1b 0 0 1b 19*0 1b 0 1b 1b 0 0 1b 1b 1b
  //   18*0 1b 1b 1b 0 0 0 1b 9*0 1b 9*0 1b 7*0 1b 0 1b 0 0 0 1b 0 1b 7*0 1b 0 0 0 1b 1b 0 1b 5*0 1b 1b 0
  //   1b 12*0 1b 1b 0 0 0 1b 0 1b 18*0 4*1b 22*0 1b 0 1b 1b 12*0 1b 1b 1b 0 0 0 1b 1b 1b 8*0 1b 7*0 1b 9*0
  //   1b 0 1b 7*0 1b 0 0 0 4*1b 4*0 1b 9*0 1b 4*0 1b 6*0 1b 0 0 1b 0 0 1b 9*0 1b 11*0 1b 0 0 1b 1b 1b 6*0
  //   1b 5*0 1b 0 0 0 1b 0 1b 0 0 0 1b 0 1b 0 1b 5*0 1b 0 0 0 1b 0 1b 1b 14*0 1b 0 0 1b 9*0 1b 0 0 1b 1b 0
  //   1b 9*0 1b 9*0 1b 0 0 0 1b 8*0 1b 0 1b 1b 0 0 1b 1b 13*0 1b 5*0 1b 1b 1b 0 1b 13*0 1b 0 0 0 1b 0 0 1b
  //   1b 1b 4*0 1b 9*0 1b 0 1b 0 0 1b 4*0 1b 28*0 1b 1b 1b 0 0 1b 9*0 1b 6*0 1b 4*0 1b 1b 13*0 1b 1b 1b
  //   4*0 1b 6*0 1b 0 0 1b 0 0 1b 6*0 1b 7*0 1b 0 1b 0 0 0 1b 1b 15*0 1b 0 1b 1b 0 0 1b 0 1b 0 1b 21*0 1b
  //   0 0 0 1b 9*0 1b 0 1b 1b 1b 5*0 1b 5*0 1b 11*0 1b 1b 0 0 0 4*1b 5*0 1b 1b 12*0 1b 0 0 0 1b 1b 1b 0 1b
  //   22*0 1b 0 0 1b 0 0 1b 1b 0 0 1b 9*0 1b 0 0 1b 1b 1b 4*0 1b 0 0 1b 4*0 1b 4*0 1b 14*0 1b 1b 0 0 1b
  //   17*0 1b 0 0 0 1b 5*0 1b 5*0 1b 5*0 1b 0 0 0 1b 0 0 0 1b 0 1b 0 0 0 1b 0 1b 0 1b 0 1b 5*0 1b 7*0 1b 0
  //   1b 5*0 1b 0 0 0 1b 5*0 1b 0 0 1b 6*0 1b 0 0 1b 0 0 0 1b 1b 1b 11*0 1b 0 1b 9*0 1b 0 1b 0 0 1b 0 1b
  //   1b 0 1b 4*0 1b 4*0 1b 4*0 1b 13*0 1b 6*0 1b 14*0 1b 0 0 0 1b 1b 1b 0 0 0 1b 7*0 1b 0 1b 5*0 1b 0 1b
  //   0 1b 0 0 1b 4*0 1b 4*0 1b 7*0 1b 0 0 0 1b 0 1b 9*0 1b 13*0 1b 1b 1b 21*0 1b 0 0 0 1b 0 0 1b 6*0 1b
  //   4*0 1b 9*0 1b 0 0 1b 9*0 1b 0 1b 0 0 1b 1b 1b 12*0 1b 0 1b 0 0 0 1b 5*0 1b 0 0 0 1b 5*0 1b 0 0 0 1b
  //   4*0 1b 0 0 0 1b 0 0 1b 11*0 1b 1b 1b 0 0 1b 9*0 1b 0 0 0 1b 9*0 1b 16*0 1b 9*0 1b 0 1b 0 1b 0 0 1b 0
  //   0 1b 0 1b 0 1b 5*0 1b 0 1b 0 0 1b 5*0 1b 6*0 1b 0 0 1b 9*0 1b 0 0 1b 9*0 1b 12*0 1b 1b 1b 5*0 1b 6*0
  //   1b 1b 15*0 1b 0 0 0 4*1b 0 0 1b 0 1b 15*0 1b 0 0 0 1b 1b 1b 0 0 0 1b 11*0 1b 1b 1b 11*0 1b 7*0 1b 1b
  //   0 0 4*1b 22*0 1b 1b 0 1b 0 1b 0 0 1b 5*0 1b 0 0 1b 1b 12*0 1b 1b 0 1b 20*0 1b 1b 1b 0 0 0 1b 9*0 1b
  //   1b 8*0 1b 0 0 1b 0 1b 1b 1b 0 0 1b 15*0 1b 1b 8*0 1b 1b 1b 15*0 1b 0 0 1b 0 1b 0 0 1b 6*0 1b 4*0 1b
  //   0 1b 7*0 1b 0 1b 7*0 1b 13*0 4*1b 0 0 1b 9*0 1b 0 0 1b 6*0 4*1b 0 1b 1b 1b 15*0 1b 11*0 1b 1b 1b 0 0
  //   1b 1b 20*0 1b 1b 0 0 1b 1b 0 1b 16*0 1b 1b 17*0 1b 0 1b 1b 0 0 0 1b 12*0 1b 0 1b 0 0 1b 0 1b 0 0 1b
  //   0 1b 0 0 1b 6*0 1b 0 0 1b 11*0 4*1b 13*0 1b 6*0 1b 0 0 1b 19*0 1b 5*0 1b 0 1b 0 1b 0 0 0 1b 5*0 1b
  //   9*0 1b 16*0 1b 14*0 1b 1b 1b 0 1b 1b 1b 9*0 1b 0 1b 1b 0 0 0 1b 1b 1b 16*0 1b 0 0 1b 1b 0 0 0 1b 0
  //   1b 7*0 1b 5*0 1b 1b 0 0 1b 4*0 1b 4*0 1b 12*0 1b 0 0 1b 1b 1b 4*0 1b 0 1b 4*0 1b 0 0 1b 0 0 0 1b
  //   15*0 1b 6*0 1b 7*0 1b 6*0 1b 0 0 1b 6*0 1b 1b 0 1b 0 1b 0 1b 1b 4*0 1b 0 1b 9*0 1b 12*0 1b 1b 1b
  //   11*0 1b 1b 0 0 0 1b 8*0 1b 1b 1b 14*0 1b 0 0 0 1b 5*0 1b 9*0 1b 5*0 1b 1b 1b 0 1b 0 0 1b 20*0 1b 1b
  //   1b 0 0 0 1b 1b 12*0 1b 1b 0 1b 6*0 1b 0 0 1b 6*0 1b 0 0 0 1b 8*0 1b 13*0 4*1b 11*0 1b 1b 12*0 1b 1b
  //   1b 0 1b 1b 1b 17*0 1b 1b 0 1b 13*0 1b 0 1b 1b 0 1b 0 1b 7*0 1b 0 1b 9*0 1b 6*0 1b 4*0 1b 1b 0 1b
  //   12*0 1b 0 0 1b 1b 1b 12*0 4*1b 11*0 1b 0 0 0 1b 5*0 1b 9*0 1b 0 0 0 1b 1b 20*0 1b 1b 4*0 1b 9*0 1b 0
  //   1b 0 0 1b 0 0 1b 15*0 4*1b 0 0 1b 1b 1b 4*0 1b 1b 6*0 1b 6*0 1b 0 0 1b 0 0 1b 6*0 1b 6*0 1b 0 0 1b 0
  //   1b 0 0 1b 0 1b 4*0 1b 9*0 1b 8*0 1b 4*0 1b 1b 1b 4*0 1b 9*0 1b 9*0 1b 0 1b 0 1b 1b 1b 5*0 1b 6*0 1b
  //   0 0 1b 0 0 1b 0 0 0 1b 0 0 1b 21*0 1b 5*0 1b 1b 16*0 1b 1b 1b 5*0 1b 6*0 1b 0 0 1b 9*0 4*1b 0 1b 1b
  //   0 1b 22*0 1b 0 0 1b 0 0 0 1b 0 0 1b 0 0 1b 17*0 1b 0 1b 1b 1b 5*0 1b 7*0 1b 0 1b 0 0 0 1b 11*0 1b 0
  //   0 0 1b 5*0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
endmodule

module random_number (
  input  cl,
  input  update_random_number_for_field,
  output [7:0] cell_data
);

  wire [7:0] divider_1_rem, random_1_out;

  Random random_1 (.clk(cl), .out(random_1_out));  // open: next, clr
  Divider divider_1 (.a(random_1_out), .b(8'h64), .rem(divider_1_rem));  // open: out, upper
  Register register_1 (.D(divider_1_rem), .Q(cell_data), .clk(update_random_number_for_field));  // open: en, clr
endmodule

module display_ship (
  input  [1:0] num_picture,
  output [19:0] out_2,
  output [19:0] out_3,
  output [19:0] out_4,
  output [19:0] out_5,
  output [19:0] out_6,
  output [19:0] out_7,
  output [19:0] out_8,
  output [19:0] out_9,
  output [19:0] out_10,
  output [19:0] out_11,
  output [19:0] out_12,
  output [19:0] out_13,
  output [19:0] out_14,
  output [19:0] out_15,
  output [19:0] out_16,
  output [19:0] out_17,
  output [19:0] out_18,
  output [19:0] out_19,
  output [19:0] out_20,
  output [19:0] out_21,
  output [19:0] out_22,
  output [19:0] out_23,
  output [19:0] out_24,
  output [19:0] out_25,
  output [19:0] out_26,
  output [19:0] out_27,
  output [19:0] out_28,
  output [19:0] out_29,
  output [19:0] out_30,
  output [19:0] out_31,
  output [19:0] out_32,
  output [19:0] out_33
);

  wire is_1, is_2, is_3, is_4;
  wire [3:1] _1_5, _1_7, _1_8, _1_10, _1_11, _1_14, _1_16, _1_17, _1_19, _1_20, _1_22, _1_23;
  wire [3:3] _1_4, _1_29;
  wire [4:2] _3_27, _3_28, _3_29, _3_30, _3_31, _4_2, _4_3, _4_4, _4_5, _4_6;
  wire [5:1] _1_6, _1_9, _1_12, _1_15, _1_18, _1_21;
  wire [5:3] _1_3, _1_30;
  wire [9:1] _1_13;
  wire [9:9] _1_2;
  wire [13:1] _1_24, _1_25, _1_26, _1_27, _1_28;
  wire [17:17] _2_9;
  wire [18:18] _2_10;
  wire [19:0] _2_5, _2_28;
  wire [19:1] _2_4, _2_29;
  wire [19:2] _2_3, _2_30;
  wire [19:3] _2_2, _2_31;
  wire [19:4] _2_1, _2_32;
  wire [19:8] _2_18, _2_19, _2_20;
  wire [19:15] _2_7;
  wire [19:16] _2_8;
  wire [19:19] _2_6, _2_11, _2_12, _2_13, _2_14, _2_15, _2_16, _2_17, _2_21, _2_22, _2_23, _2_24, _2_25,
       _2_26, _2_27;

  assign out_2 = is_1 ? 20'h60 : 20'bz;  // Controlled_Buffer controlled_buffer_1
  assign out_2 = is_2 ? {{13{_2_1[19]}}, 2'b11, {5{_2_1[4]}}} : 20'bz;  // Controlled_Buffer controlled_buffer_2
  assign out_2 = is_3 ? {20{1'b0}} : 20'bz;  // Controlled_Buffer controlled_buffer_3
  assign out_2 = is_4 ? 20'h200 : 20'bz;  // Controlled_Buffer controlled_buffer_4
  assign out_3 = is_1 ? {{10{1'b0}}, _1_2[9], 9'h70} : 20'bz;  // Controlled_Buffer controlled_buffer_5
  assign out_3 = is_2 ? {{13{_2_2[19]}}, 3'b111, {4{_2_2[3]}}} : 20'bz;  // Controlled_Buffer controlled_buffer_6
  assign out_3 = is_3 ? 20'h7e790 : 20'bz;  // Controlled_Buffer controlled_buffer_7
  assign out_3 = is_4 ? {15'h1019, _4_2[4], 1'b1, _4_2[2], 2'b11} : 20'bz;  // Controlled_Buffer controlled_buffer_8
  assign out_4 = is_1 ? {14'h9, _1_3[5], 1'b1, _1_3[3], 3'b000} : 20'bz;  // Controlled_Buffer controlled_buffer_9
  assign out_4 = is_2 ? {{13{_2_3[19]}}, 4'b1010, {3{_2_3[2]}}} : 20'bz;  // Controlled_Buffer controlled_buffer_10
  assign out_4 = is_3 ? 20'h52490 : 20'bz;  // Controlled_Buffer controlled_buffer_11
  assign out_4 = is_4 ? {15'h100d, _4_3[4], 1'b1, _4_3[2], 2'b11} : 20'bz;  // Controlled_Buffer controlled_buffer_12
  assign out_5 = is_1 ? {16'h2f, _1_4[3], 3'b100} : 20'bz;  // Controlled_Buffer controlled_buffer_13
  assign out_5 = is_2 ? {{13{_2_4[19]}}, 5'b11101, {2{_2_4[1]}}} : 20'bz;  // Controlled_Buffer controlled_buffer_14
  assign out_5 = is_3 ? 20'h52490 : 20'bz;  // Controlled_Buffer controlled_buffer_15
  assign out_5 = is_4 ? {15'h1fc5, _4_4[4], 1'b1, _4_4[2], 2'b11} : 20'bz;  // Controlled_Buffer controlled_buffer_16
  assign out_6 = is_1 ? {16'h3f, _1_5[3], 1'b1, _1_5[1], 1'b0} : 20'bz;  // Controlled_Buffer controlled_buffer_17
  assign out_6 = is_2 ? {{5{_2_5[19]}}, 14'h2bfa, _2_5[0]} : 20'bz;  // Controlled_Buffer controlled_buffer_18
  assign out_6 = is_3 ? 20'h2c4f0 : 20'bz;  // Controlled_Buffer controlled_buffer_19
  assign out_6 = is_4 ? {15'h1001, _4_5[4], 1'b1, _4_5[2], 2'b11} : 20'bz;  // Controlled_Buffer controlled_buffer_20
  assign out_7 = is_1 ? {14'h1f, _1_6[5], 1'b1, _1_6[3], 1'b1, _1_6[1], 1'b1} : 20'bz;  // Controlled_Buffer controlled_buffer_21
  assign out_7 = is_2 ? {{5{_2_6[19]}}, 15'h57d5} : 20'bz;  // Controlled_Buffer controlled_buffer_22
  assign out_7 = is_3 ? {20{1'b0}} : 20'bz;  // Controlled_Buffer controlled_buffer_23
  assign out_7 = is_4 ? {15'h1001, _4_6[4], 1'b1, _4_6[2], 2'b11} : 20'bz;  // Controlled_Buffer controlled_buffer_24
  assign out_8 = is_1 ? {16'h7f, _1_7[3], 1'b1, _1_7[1], 1'b1} : 20'bz;  // Controlled_Buffer controlled_buffer_25
  assign out_8 = is_2 ? {{2{_2_7[19]}}, 2'b11, _2_7[15], 15'h57f5} : 20'bz;  // Controlled_Buffer controlled_buffer_26
  assign out_8 = is_3 ? {20{1'b0}} : 20'bz;  // Controlled_Buffer controlled_buffer_27
  assign out_8 = is_4 ? {20{1'b0}} : 20'bz;  // Controlled_Buffer controlled_buffer_28
  assign out_9 = is_1 ? {16'h3f, _1_8[3], 1'b1, _1_8[1], 1'b1} : 20'bz;  // Controlled_Buffer controlled_buffer_29
  assign out_9 = is_2 ? {_2_8[19], 2'b11, {2{_2_8[16]}}, 15'h57f5} : 20'bz;  // Controlled_Buffer controlled_buffer_30
  assign out_9 = is_3 ? 20'h1e7f0 : 20'bz;  // Controlled_Buffer controlled_buffer_31
  assign out_9 = is_4 ? 20'h3f800 : 20'bz;  // Controlled_Buffer controlled_buffer_32
  assign out_10 = is_1 ? {14'h3, _1_9[5], 1'b1, _1_9[3], 1'b1, _1_9[1], 1'b1} : 20'bz;  // Controlled_Buffer controlled_buffer_33
  assign out_10 = is_2 ? {2'b11, {3{_2_9[17]}}, 15'h57d5} : 20'bz;  // Controlled_Buffer controlled_buffer_34
  assign out_10 = is_3 ? 20'h28080 : 20'bz;  // Controlled_Buffer controlled_buffer_35
  assign out_10 = is_4 ? 20'h4000 : 20'bz;  // Controlled_Buffer controlled_buffer_36
  assign out_11 = is_1 ? {16'h7, _1_10[3], 1'b1, _1_10[1], 1'b1} : 20'bz;  // Controlled_Buffer controlled_buffer_37
  assign out_11 = is_2 ? {1'b1, {12{_2_10[18]}}, 7'b1110101} : 20'bz;  // Controlled_Buffer controlled_buffer_38
  assign out_11 = is_3 ? 20'h3e080 : 20'bz;  // Controlled_Buffer controlled_buffer_39
  assign out_11 = is_4 ? 20'h4000 : 20'bz;  // Controlled_Buffer controlled_buffer_40
  assign out_12 = is_1 ? {16'h7, _1_11[3], 1'b1, _1_11[1], 1'b1} : 20'bz;  // Controlled_Buffer controlled_buffer_41
  assign out_12 = is_2 ? {{13{_2_11[19]}}, 7'b1110101} : 20'bz;  // Controlled_Buffer controlled_buffer_42
  assign out_12 = is_3 ? 20'h7f0 : 20'bz;  // Controlled_Buffer controlled_buffer_43
  assign out_12 = is_4 ? 20'h4000 : 20'bz;  // Controlled_Buffer controlled_buffer_44
  assign out_13 = is_1 ? {14'h1, _1_12[5], 1'b1, _1_12[3], 1'b1, _1_12[1], 1'b1} : 20'bz;  // Controlled_Buffer controlled_buffer_45
  assign out_13 = is_2 ? {{13{_2_12[19]}}, 7'b1010101} : 20'bz;  // Controlled_Buffer controlled_buffer_46
  assign out_13 = is_3 ? 20'h20000 : 20'bz;  // Controlled_Buffer controlled_buffer_47
  assign out_13 = is_4 ? 20'h3f800 : 20'bz;  // Controlled_Buffer controlled_buffer_48
  assign out_14 = is_1 ? {{10{1'b0}}, _1_13[9], 5'b00111, _1_13[3], 1'b1, _1_13[1], 1'b1} : 20'bz;  // Controlled_Buffer controlled_buffer_49
  assign out_14 = is_2 ? {{12{_2_13[19]}}, 8'hf5} : 20'bz;  // Controlled_Buffer controlled_buffer_50
  assign out_14 = is_3 ? 20'h3e000 : 20'bz;  // Controlled_Buffer controlled_buffer_51
  assign out_14 = is_4 ? {20{1'b0}} : 20'bz;  // Controlled_Buffer controlled_buffer_52
  assign out_15 = is_1 ? {16'h27, _1_14[3], 1'b1, _1_14[1], 1'b1} : 20'bz;  // Controlled_Buffer controlled_buffer_53
  assign out_15 = is_2 ? {{10{_2_14[19]}}, 10'h3f5} : 20'bz;  // Controlled_Buffer controlled_buffer_54
  assign out_15 = is_3 ? 20'h20410 : 20'bz;  // Controlled_Buffer controlled_buffer_55
  assign out_15 = is_4 ? 20'h3fbf8 : 20'bz;  // Controlled_Buffer controlled_buffer_56
  assign out_16 = is_1 ? {14'hb, _1_15[5], 1'b1, _1_15[3], 1'b1, _1_15[1], 1'b1} : 20'bz;  // Controlled_Buffer controlled_buffer_57
  assign out_16 = is_2 ? {{9{_2_15[19]}}, 11'h7d5} : 20'bz;  // Controlled_Buffer controlled_buffer_58
  assign out_16 = is_3 ? 20'h410 : 20'bz;  // Controlled_Buffer controlled_buffer_59
  assign out_16 = is_4 ? 20'h24a48 : 20'bz;  // Controlled_Buffer controlled_buffer_60
  assign out_17 = is_1 ? {16'h3f, _1_16[3], 1'b1, _1_16[1], 1'b1} : 20'bz;  // Controlled_Buffer controlled_buffer_61
  assign out_17 = is_2 ? {{9{_2_16[19]}}, 11'h7f5} : 20'bz;  // Controlled_Buffer controlled_buffer_62
  assign out_17 = is_3 ? 20'h207f0 : 20'bz;  // Controlled_Buffer controlled_buffer_63
  assign out_17 = is_4 ? 20'h24a48 : 20'bz;  // Controlled_Buffer controlled_buffer_64
  assign out_18 = is_1 ? {16'h7f, _1_17[3], 1'b1, _1_17[1], 1'b1} : 20'bz;  // Controlled_Buffer controlled_buffer_65
  assign out_18 = is_2 ? {{10{_2_17[19]}}, 10'h3f5} : 20'bz;  // Controlled_Buffer controlled_buffer_66
  assign out_18 = is_3 ? 20'h3e410 : 20'bz;  // Controlled_Buffer controlled_buffer_67
  assign out_18 = is_4 ? 20'h24a48 : 20'bz;  // Controlled_Buffer controlled_buffer_68
  assign out_19 = is_1 ? {14'h1f, _1_18[5], 1'b1, _1_18[3], 1'b1, _1_18[1], 1'b1} : 20'bz;  // Controlled_Buffer controlled_buffer_69
  assign out_19 = is_2 ? {{10{_2_18[19]}}, 1'b1, _2_18[8], 8'hd5} : 20'bz;  // Controlled_Buffer controlled_buffer_70
  assign out_19 = is_3 ? 20'h20410 : 20'bz;  // Controlled_Buffer controlled_buffer_71
  assign out_19 = is_4 ? 20'h24a48 : 20'bz;  // Controlled_Buffer controlled_buffer_72
  assign out_20 = is_1 ? {16'h3f, _1_19[3], 1'b1, _1_19[1], 1'b1} : 20'bz;  // Controlled_Buffer controlled_buffer_73
  assign out_20 = is_2 ? {{10{_2_19[19]}}, 1'b1, {2{_2_19[8]}}, 7'b1110101} : 20'bz;  // Controlled_Buffer controlled_buffer_74
  assign out_20 = is_3 ? {20{1'b0}} : 20'bz;  // Controlled_Buffer controlled_buffer_75
  assign out_20 = is_4 ? {20{1'b0}} : 20'bz;  // Controlled_Buffer controlled_buffer_76
  assign out_21 = is_1 ? {16'hf, _1_20[3], 1'b1, _1_20[1], 1'b1} : 20'bz;  // Controlled_Buffer controlled_buffer_77
  assign out_21 = is_2 ? {{10{_2_20[19]}}, 1'b0, {2{_2_20[8]}}, 7'b1110101} : 20'bz;  // Controlled_Buffer controlled_buffer_78
  assign out_21 = is_3 ? 20'h3e000 : 20'bz;  // Controlled_Buffer controlled_buffer_79
  assign out_21 = is_4 ? 20'h3f8 : 20'bz;  // Controlled_Buffer controlled_buffer_80
  assign out_22 = is_1 ? {14'h1, _1_21[5], 1'b1, _1_21[3], 1'b1, _1_21[1], 1'b1} : 20'bz;  // Controlled_Buffer controlled_buffer_81
  assign out_22 = is_2 ? {{13{_2_21[19]}}, 7'b1010101} : 20'bz;  // Controlled_Buffer controlled_buffer_82
  assign out_22 = is_3 ? 20'h27f0 : 20'bz;  // Controlled_Buffer controlled_buffer_83
  assign out_22 = is_4 ? 20'h80 : 20'bz;  // Controlled_Buffer controlled_buffer_84
  assign out_23 = is_1 ? {16'h7, _1_22[3], 1'b1, _1_22[1], 1'b1} : 20'bz;  // Controlled_Buffer controlled_buffer_85
  assign out_23 = is_2 ? {{13{_2_22[19]}}, 7'b1110101} : 20'bz;  // Controlled_Buffer controlled_buffer_86
  assign out_23 = is_3 ? 20'h480 : 20'bz;  // Controlled_Buffer controlled_buffer_87
  assign out_23 = is_4 ? 20'h40 : 20'bz;  // Controlled_Buffer controlled_buffer_88
  assign out_24 = is_1 ? {16'h8007, _1_23[3], 1'b1, _1_23[1], 1'b1} : 20'bz;  // Controlled_Buffer controlled_buffer_89
  assign out_24 = is_2 ? {{13{_2_23[19]}}, 7'b1110101} : 20'bz;  // Controlled_Buffer controlled_buffer_90
  assign out_24 = is_3 ? 20'h3e480 : 20'bz;  // Controlled_Buffer controlled_buffer_91
  assign out_24 = is_4 ? 20'h20 : 20'bz;  // Controlled_Buffer controlled_buffer_92
  assign out_25 = is_1 ? {6'b110001, _1_24[13], 1'b1, _1_24[11], {5{1'b1}}, _1_24[5], 1'b1, _1_24[3], 1'b1, _1_24[1], 1'b1} : 20'bz;  // Controlled_Buffer controlled_buffer_93
  assign out_25 = is_2 ? {{12{_2_24[19]}}, 8'hd5} : 20'bz;  // Controlled_Buffer controlled_buffer_94
  assign out_25 = is_3 ? 20'h2a780 : 20'bz;  // Controlled_Buffer controlled_buffer_95
  assign out_25 = is_4 ? 20'h3f8 : 20'bz;  // Controlled_Buffer controlled_buffer_96
  assign out_26 = is_1 ? {6'b011001, _1_25[13], 1'b1, _1_25[11], {7{1'b1}}, _1_25[3], 1'b1, _1_25[1], 1'b1} : 20'bz;  // Controlled_Buffer controlled_buffer_97
  assign out_26 = is_2 ? {{10{_2_25[19]}}, 10'h3f5} : 20'bz;  // Controlled_Buffer controlled_buffer_98
  assign out_26 = is_3 ? {20{1'b0}} : 20'bz;  // Controlled_Buffer controlled_buffer_99
  assign out_26 = is_4 ? {20{1'b0}} : 20'bz;  // Controlled_Buffer controlled_buffer_100
  assign out_27 = is_1 ? {6'b001101, _1_26[13], 1'b1, _1_26[11], {7{1'b1}}, _1_26[3], 1'b1, _1_26[1], 1'b1} : 20'bz;  // Controlled_Buffer controlled_buffer_101
  assign out_27 = is_2 ? {{9{_2_26[19]}}, 11'h7f5} : 20'bz;  // Controlled_Buffer controlled_buffer_102
  assign out_27 = is_3 ? {20{1'b0}} : 20'bz;  // Controlled_Buffer controlled_buffer_103
  assign out_27 = is_4 ? 20'h3f8 : 20'bz;  // Controlled_Buffer controlled_buffer_104
  assign out_28 = is_1 ? {6'b000001, _1_27[13], 1'b1, _1_27[11], {5{1'b1}}, _1_27[5], 1'b1, _1_27[3], 1'b1, _1_27[1], 1'b1} : 20'bz;  // Controlled_Buffer controlled_buffer_105
  assign out_28 = is_2 ? {{9{_2_27[19]}}, 11'h7d5} : 20'bz;  // Controlled_Buffer controlled_buffer_106
  assign out_28 = is_3 ? {15'h1, _3_27[4], 1'b1, _3_27[2], 2'b11} : 20'bz;  // Controlled_Buffer controlled_buffer_107
  assign out_28 = is_4 ? 20'h208 : 20'bz;  // Controlled_Buffer controlled_buffer_108
  assign out_29 = is_1 ? {6'b000001, _1_28[13], 1'b1, _1_28[11], {7{1'b1}}, _1_28[3], 1'b1, _1_28[1], 1'b0} : 20'bz;  // Controlled_Buffer controlled_buffer_109
  assign out_29 = is_2 ? {{10{_2_28[19]}}, 9'h1fa, _2_28[0]} : 20'bz;  // Controlled_Buffer controlled_buffer_110
  assign out_29 = is_3 ? {15'h1, _3_28[4], 1'b1, _3_28[2], 2'b11} : 20'bz;  // Controlled_Buffer controlled_buffer_111
  assign out_29 = is_4 ? 20'h208 : 20'bz;  // Controlled_Buffer controlled_buffer_112
  assign out_30 = is_1 ? {16'h7, _1_29[3], 3'b100} : 20'bz;  // Controlled_Buffer controlled_buffer_113
  assign out_30 = is_2 ? {{10{_2_29[19]}}, 1'b1, _2_29[8], 6'b111101, {2{_2_29[1]}}} : 20'bz;  // Controlled_Buffer controlled_buffer_114
  assign out_30 = is_3 ? {15'h5, _3_29[4], 1'b1, _3_29[2], 2'b11} : 20'bz;  // Controlled_Buffer controlled_buffer_115
  assign out_30 = is_4 ? 20'h208 : 20'bz;  // Controlled_Buffer controlled_buffer_116
  assign out_31 = is_1 ? {14'h1, _1_30[5], 1'b1, _1_30[3], 3'b000} : 20'bz;  // Controlled_Buffer controlled_buffer_117
  assign out_31 = is_2 ? {{10{_2_30[19]}}, 1'b1, {2{_2_30[8]}}, 4'b1010, {3{_2_30[2]}}} : 20'bz;  // Controlled_Buffer controlled_buffer_118
  assign out_31 = is_3 ? {15'hd, _3_30[4], 1'b1, _3_30[2], 2'b11} : 20'bz;  // Controlled_Buffer controlled_buffer_119
  assign out_31 = is_4 ? 20'h1f0 : 20'bz;  // Controlled_Buffer controlled_buffer_120
  assign out_32 = is_1 ? 20'h70 : 20'bz;  // Controlled_Buffer controlled_buffer_121
  assign out_32 = is_2 ? {{10{_2_31[19]}}, 1'b0, {2{_2_31[8]}}, 3'b111, {4{_2_31[3]}}} : 20'bz;  // Controlled_Buffer controlled_buffer_122
  assign out_32 = is_3 ? {15'h19, _3_31[4], 1'b1, _3_31[2], 2'b11} : 20'bz;  // Controlled_Buffer controlled_buffer_123
  assign out_32 = is_4 ? {20{1'b0}} : 20'bz;  // Controlled_Buffer controlled_buffer_124
  assign out_33 = is_1 ? 20'h60 : 20'bz;  // Controlled_Buffer controlled_buffer_125
  assign out_33 = is_2 ? {{13{_2_32[19]}}, 2'b11, {5{_2_32[4]}}} : 20'bz;  // Controlled_Buffer controlled_buffer_126
  assign out_33 = is_3 ? 20'h600 : 20'bz;  // Controlled_Buffer controlled_buffer_127
  assign out_33 = is_4 ? {20{1'b0}} : 20'bz;  // Controlled_Buffer controlled_buffer_128
  Demultiplexer #(.select(2), .enable("false")) demultiplexer_1 (
    .out0(is_3), .out1(is_1), .out2(is_2), .out3(is_4), .in(1'b1), .sel(num_picture));

  // Other names for the same wires on the sheet: _2_1 (some bits) = {{12{_2_1[19]}}, {4{_2_1[4]}}};
  //   _2_2 (some bits) = {{12{_2_2[19]}}, {3{_2_2[3]}}}; _2_3 (some bits) = {{12{_2_3[19]}}, {2{_2_3[2]}}};
  //   _2_4 (some bits) = {{12{_2_4[19]}}, _2_4[1]}; _2_5[18:15] = {4{_2_5[19]}}; _2_6[18:15] = {4{_2_6[19]}};
  //   _2_7[18] = _2_7[19]; _2_8[15] = _2_8[16]; _2_9[16:15] = {2{_2_9[17]}}; _2_10[17:7] = {11{_2_10[18]}};
  //   _2_11[18:7] = {12{_2_11[19]}}; _2_12[18:7] = {12{_2_12[19]}}; _2_13[18:8] = {11{_2_13[19]}};
  //   _2_14[18:10] = {9{_2_14[19]}}; _2_15[18:11] = {8{_2_15[19]}}; _2_16[18:11] = {8{_2_16[19]}};
  //   _2_17[18:10] = {9{_2_17[19]}}; _2_18[18:10] = {9{_2_18[19]}}; _2_19 (some bits) = {{9{_2_19[19]}}, _2_19[8]};
  //   _2_20 (some bits) = {{9{_2_20[19]}}, _2_20[8]}; _2_21[18:7] = {12{_2_21[19]}}; _2_22[18:7] = {12{_2_22[19]}};
  //   _2_23[18:7] = {12{_2_23[19]}}; _2_24[18:8] = {11{_2_24[19]}}; _2_25[18:10] = {9{_2_25[19]}};
  //   _2_26[18:11] = {8{_2_26[19]}}; _2_27[18:11] = {8{_2_27[19]}}; _2_28[18:10] = {9{_2_28[19]}};
  //   _2_29 (some bits) = {{9{_2_29[19]}}, _2_29[1]}; _2_30 (some bits) = {{9{_2_30[19]}}, _2_30[8], {2{_2_30[2]}}};
  //   _2_31 (some bits) = {{9{_2_31[19]}}, _2_31[8], {3{_2_31[3]}}};
  //   _2_32 (some bits) = {{12{_2_32[19]}}, {4{_2_32[4]}}}
endmodule
